# Fritzing sketch Diagrama de conexión (saved by Fritzing 0.9.6b)
breadboards: 1

parts:
  Componente1 = Arduino Uno (Rev3)
  J1 = Piezo Speaker
  RHT1 = Humidity and Temperature Sensor RHT03
  Water_Level_Sensor1 = Water Level Sensor
  S2 = Momentary Switch [package=ksa_sealed_tac_switch]
  R1 = Resistor [tolerance=±5% power=0.25 resistance=330 package=THT]
  U1 = LCD-16X2 [package=lcd-16x2]
  U2 = POT [package=pot_alpha_rv16af-20]
  R2 = Resistor [tolerance=±5% power=0.25 resistance=100 package=THT]

nets:
  N1: Componente1.A0, Water_Level_Sensor1.SIG
  N2: Componente1.D8, S2.3, R1.Pin_1
  N3: Componente1.D9_PWM, J1.pin2
  N4: Componente1.D11_PWM/MOSI, U1.E
  N5: Componente1.D12/MISO, U1.RS
  N6: Componente1.D2, U1.DB7
  N7: Componente1.D3_PWM, U1.DB6
  N8: Componente1.D4, U1.DB5
  N9: Componente1.D5_PWM, U1.DB4
  N10: Componente1.D7, RHT1.Data-signal
  VCC: Componente1.5V, RHT1.Vcc, Water_Level_Sensor1.VCC, S2.1, U2.E, R2.Pin_0
  GND: Componente1.GND, J1.pin1, RHT1.GND_1, RHT1.GND_2, Water_Level_Sensor1.GND, R1.Pin_0
  N11: U1.VO, U2.S
  N12: U1.A, R2.Pin_1
  N13: U1.K, U2.A

notes:
  10K ohm

custom parts:
  Water Level Sensor: A water level sensor. This sensor operates at 3V to 5V. The Sig (signal) pin outputs an analogue signal that is in proportion to the amount of water in contact with the sensor.
